// Logisim project Project.circ as structural Verilog
module _1bit_Alu (
  input  A,
  input  B,
  input  [1:0] select_bits,
  input  cin,
  input  borrow_in,
  output Result,
  output carry_out
);

  wire adder_1_cout, adder_1_out, and_1_out, and_2_out, and_3_out, or_1_out, subtractor_1_bout,
       subtractor_1_out;

  and and_1 (and_1_out, A, B);
  or or_1 (or_1_out, A, B);
  Adder #(.width(1)) adder_1 (.a(A), .b(B), .out(adder_1_out), .cin(cin), .cout(adder_1_cout));
  Subtractor #(.width(1)) subtractor_1 (
    .a(A), .b(B), .out(subtractor_1_out), .bin(borrow_in), .bout(subtractor_1_bout));
  Multiplexer #(.select(2)) multiplexer_1 (
    .in0(and_1_out), .in1(or_1_out), .in2(adder_1_out), .in3(subtractor_1_out), .out(Result),
    .sel(select_bits));  // open: en
  and and_2 (and_2_out, select_bits[1], adder_1_cout);
  and and_3 (and_3_out, select_bits[1], subtractor_1_bout);
  Multiplexer multiplexer_2 (.in0(and_2_out), .in1(and_3_out), .out(carry_out), .sel(select_bits[0]));  // open: en

  // Notes on the sheet:
  //   ISA format
  //   000 = AND
  //   001 = OR
  //   010 = ADD
  //   011 = Subtract
endmodule

// ALU
module _10_bit_alu (
  input  [9:0] A,
  input  [9:0] B,
  input  C_in,
  input  Borrow_in,
  input  [1:0] Op_code,
  output [9:0] Result,
  output Zero,
  output C_out
);

  wire n1bit_alu_1_carry_out, n1bit_alu_3_carry_out, n1bit_alu_4_carry_out, n1bit_alu_5_carry_out,
       n1bit_alu_6_carry_out, n1bit_alu_7_carry_out, n1bit_alu_8_carry_out, n1bit_alu_9_carry_out,
       n1bit_alu_10_carry_out;

  _1bit_Alu u_1bit_alu_1 (
    .A(A[0]), .B(B[0]), .cin(C_in), .borrow_in(Borrow_in), .select_bits(Op_code), .Result(Result[0]),
    .carry_out(n1bit_alu_1_carry_out));
  _1bit_Alu u_1bit_alu_2 (
    .A(A[9]), .B(B[9]), .cin(n1bit_alu_4_carry_out), .borrow_in(n1bit_alu_4_carry_out),
    .select_bits(Op_code), .Result(Result[9]), .carry_out(C_out));
  _1bit_Alu u_1bit_alu_3 (
    .A(A[1]), .B(B[1]), .cin(n1bit_alu_1_carry_out), .borrow_in(n1bit_alu_1_carry_out),
    .select_bits(Op_code), .Result(Result[1]), .carry_out(n1bit_alu_3_carry_out));
  _1bit_Alu u_1bit_alu_4 (
    .A(A[8]), .B(B[8]), .cin(n1bit_alu_6_carry_out), .borrow_in(n1bit_alu_6_carry_out),
    .select_bits(Op_code), .Result(Result[8]), .carry_out(n1bit_alu_4_carry_out));
  _1bit_Alu u_1bit_alu_5 (
    .A(A[2]), .B(B[2]), .cin(n1bit_alu_3_carry_out), .borrow_in(n1bit_alu_3_carry_out),
    .select_bits(Op_code), .Result(Result[2]), .carry_out(n1bit_alu_5_carry_out));
  _1bit_Alu u_1bit_alu_6 (
    .A(A[7]), .B(B[7]), .cin(n1bit_alu_8_carry_out), .borrow_in(n1bit_alu_8_carry_out),
    .select_bits(Op_code), .Result(Result[7]), .carry_out(n1bit_alu_6_carry_out));
  _1bit_Alu u_1bit_alu_7 (
    .A(A[3]), .B(B[3]), .cin(n1bit_alu_5_carry_out), .borrow_in(n1bit_alu_5_carry_out),
    .select_bits(Op_code), .Result(Result[3]), .carry_out(n1bit_alu_7_carry_out));
  _1bit_Alu u_1bit_alu_8 (
    .A(A[6]), .B(B[6]), .cin(n1bit_alu_10_carry_out), .borrow_in(n1bit_alu_10_carry_out),
    .select_bits(Op_code), .Result(Result[6]), .carry_out(n1bit_alu_8_carry_out));
  _1bit_Alu u_1bit_alu_9 (
    .A(A[4]), .B(B[4]), .cin(n1bit_alu_7_carry_out), .borrow_in(n1bit_alu_7_carry_out),
    .select_bits(Op_code), .Result(Result[4]), .carry_out(n1bit_alu_9_carry_out));
  _1bit_Alu u_1bit_alu_10 (
    .A(A[5]), .B(B[5]), .cin(n1bit_alu_9_carry_out), .borrow_in(n1bit_alu_9_carry_out),
    .select_bits(Op_code), .Result(Result[5]), .carry_out(n1bit_alu_10_carry_out));
  nor nor_1 (Zero, Result[0], Result[1], Result[2], Result[3], Result[4], Result[5], Result[6], Result[7], Result[9]);

  // Notes on the sheet:
  //   ISA format
  //   000 = AND
  //   001 = OR
  //   010 = ADD
  //   011 = Subtract
endmodule

// Register
module _2_bit_resiter (
  input  Register_wite,
  input  [1:0] RD,
  input  [1:0] RS,
  input  [1:0] RT,
  input  [9:0] Wright_Data,
  input  clock,
  output [9:0] Read_data_1,
  output [9:0] Read_data_2
);

  wire and_1_out, and_2_out, and_3_out, and_4_out, decoder_1_out0, decoder_1_out1, decoder_1_out2,
       decoder_1_out3;
  wire [9:0] t0_q, t1_q, t2_q, Zero_q;

  Decoder #(.select(2)) decoder_1 (
    .out0(decoder_1_out0), .out1(decoder_1_out1), .out2(decoder_1_out2), .out3(decoder_1_out3), .sel(RD));  // open: en
  and and_1 (and_1_out, Register_wite, decoder_1_out0);
  and and_2 (and_2_out, Register_wite, decoder_1_out1);
  and and_3 (and_3_out, Register_wite, decoder_1_out2);
  and and_4 (and_4_out, Register_wite, decoder_1_out3);
  Register #(.width(10)) Zero (.en(and_1_out), .Q(Zero_q), .clk(clock));  // open: D, clr
  Register #(.width(10)) t0 (.D(Wright_Data), .en(and_2_out), .Q(t0_q), .clk(clock));  // open: clr
  Register #(.width(10)) t1 (.D(Wright_Data), .en(and_3_out), .Q(t1_q), .clk(clock));  // open: clr
  Register #(.width(10)) t2 (.D(Wright_Data), .en(and_4_out), .Q(t2_q), .clk(clock));  // open: clr
  Multiplexer #(.select(2), .width(10)) multiplexer_1 (
    .in0(Zero_q), .in1(t0_q), .in2(t1_q), .in3(t2_q), .out(Read_data_1), .sel(RS));  // open: en
  Multiplexer #(.select(2), .width(10)) multiplexer_2 (
    .in0(Zero_q), .in1(t0_q), .in2(t1_q), .in3(t2_q), .out(Read_data_2), .sel(RT));  // open: en

  // Notes on the sheet:
  //   Read 1
  //   Read 2
  //   $Zero = 00, $t0 = 01, $t1= 10, $t2 = 11
endmodule

module Dtapath (
  input  Clear_PC,
  input  Clear_RAm
);

  wire and_1_out, Clock_out, main_control_block_1_alusrc, main_control_block_1_branch,
       main_control_block_1_memread, main_control_block_1_memtoreg, main_control_block_1_memwright,
       main_control_block_1_regwrite, main_control_block_1_rgdst, n10_bit_alu_1_zero;
  wire [1:0] main_control_block_1_aluop0, main_control_block_1_beqselect2, multiplexer_1_out;
  wire [3:0] adder_1_out, adder_2_out, multiplexer_3_out, PC_q;
  wire [9:0] bit_extender_1_out, multiplexer_2_out, multiplexer_4_out, n2_bit_resiter_1_read_data_1,
       n2_bit_resiter_1_read_data_2, n10_bit_alu_1_result, ram_1_data, rom_1_data;

  Clock Clock (.out(Clock_out));
  Register #(.width(4)) PC (.D(multiplexer_3_out), .Q(PC_q), .clk(Clock_out), .clr(Clear_PC));  // open: en
  Adder #(.width(4)) adder_1 (.a(PC_q), .b(4'b0001), .out(adder_1_out));  // open: cin, cout
  ROM #(.addrWidth(4), .dataWidth(10)) rom_1 (.addr(PC_q), .data(rom_1_data));  // open: sel
  Main_Control_Block main_control_block_1 (
    .Op_0(rom_1_data[9]), .Op1(rom_1_data[8]), .Op2(rom_1_data[6]), .Op3(rom_1_data[7]),
    .RgDst(main_control_block_1_rgdst), .AluSrc(main_control_block_1_alusrc),
    .MemToReg(main_control_block_1_memtoreg), .RegWrite(main_control_block_1_regwrite),
    .MemRead(main_control_block_1_memread), .MemWright(main_control_block_1_memwright),
    .Branch(main_control_block_1_branch), .AluOp1(main_control_block_1_aluop0[1]),
    .AluOP0(main_control_block_1_aluop0[0]), .BeqSelect1(main_control_block_1_beqselect2[1]),
    .BeqSelect2(main_control_block_1_beqselect2[0]));
  Multiplexer #(.width(2)) multiplexer_1 (
    .in0(rom_1_data[3:2]), .in1(rom_1_data[1:0]), .out(multiplexer_1_out), .sel(main_control_block_1_rgdst));  // open: en
  _2_bit_resiter u_2_bit_resiter_1 (
    .Register_wite(main_control_block_1_regwrite), .RD(rom_1_data[5:4]), .RS(rom_1_data[3:2]),
    .RT(multiplexer_1_out), .Wright_Data(multiplexer_4_out), .clock(Clock_out),
    .Read_data_1(n2_bit_resiter_1_read_data_1), .Read_data_2(n2_bit_resiter_1_read_data_2));
  assign bit_extender_1_out = {{8{1'b0}}, rom_1_data[1:0]};  // Bit_Extender bit_extender_1
  Adder #(.width(4)) adder_2 (
    .a(adder_1_out), .b({main_control_block_1_beqselect2, rom_1_data[1:0]}), .out(adder_2_out));  // open: cin, cout
  Multiplexer #(.width(10)) multiplexer_2 (
    .in0(n2_bit_resiter_1_read_data_2), .in1(bit_extender_1_out), .out(multiplexer_2_out),
    .sel(main_control_block_1_alusrc));  // open: en
  Multiplexer #(.width(4)) multiplexer_3 (
    .in0(adder_1_out), .in1(adder_2_out), .out(multiplexer_3_out), .sel(and_1_out));  // open: en
  and and_1 (and_1_out, main_control_block_1_branch, n10_bit_alu_1_zero);
  _10_bit_alu u_10_bit_alu_1 (
    .A(n2_bit_resiter_1_read_data_1), .B(multiplexer_2_out), .Op_code(main_control_block_1_aluop0),
    .Result(n10_bit_alu_1_result), .Zero(n10_bit_alu_1_zero));  // open: C_in, Borrow_in, C_out
  RAM #(.addrWidth(10), .dataWidth(10), .bus("separate")) ram_1 (
    .addr(n10_bit_alu_1_result), .din(n2_bit_resiter_1_read_data_2), .data(ram_1_data),
    .str(main_control_block_1_memwright), .clk(Clock_out), .ld(main_control_block_1_memread), .clr(Clear_RAm));  // open: sel
  Multiplexer #(.width(10)) multiplexer_4 (
    .in0(n10_bit_alu_1_result), .in1(ram_1_data), .out(multiplexer_4_out), .sel(main_control_block_1_memtoreg));  // open: en

  // Notes on the sheet:
  //   contents of rom_1 (hex, n*v repeats v):
  //   d0 20 30 226 3e 3e 3e9 103 2fc 0 2fc
  //   1, when R formate
  //   1011 = b or 0011 = 3
  //   C code :
  //   For( i=0; i<x; i++ )
  //   1, when I formate
  //   Sum = Sum + 2i;
  //   L1 :  beq $t1, $t0
  //   MIps Code :
  //   Lw $t0, 0($zero)
  //   add $t1, #zero, $ zero
  //   add $t2,$ zero, $zero
  //   add $t2, $t2, $t1
  //   add $t2, $t2, $t1
  //   beq $zero, $zero
  //   L2 :  Sw $t2, 1($zero)
  //   ISA format :
  //   000 = AND
  //   001 = OR
  //   010 = ADD
  //   011 = Subtract
  //   0011    01   00   00   =  0d0
  //   0000     10     00    00  = 020
  //   0000    11    00    00  = 030
  //   1000     10     01   10  = 226
  //   0000    11    11    10 = 03e
  //   0000   11    11    10 = 03e
  //   1111  10    10   01  =  3e9
  //   1000   00   00   11  =  103
  //   1011   11   11   00  =  2fc
  //   Operations   =   op_code
  //   R- Format   =   0000
  //   I- Format   =  1111
  //   Lode (Lw)   =   0011
  //   Store (Sw)   =   1011
  //   Beq1    =   0100
  //   Beq 2    =   1000
  //   $Zero = 00, $t0 = 01, $t1= 10, $t2 = 11
  //   Op    RD   RS   RT = HEX conversion
endmodule

// Main Control
module Main_Control_Block (
  input  Op_0,
  input  Op1,
  input  Op2,
  input  Op3,
  output RgDst,
  output AluSrc,
  output MemToReg,
  output RegWrite,
  output MemRead,
  output MemWright,
  output Branch,
  output AluOp1,
  output AluOP0,
  output BeqSelect1,
  output BeqSelect2
);

  wire I_type_out, not_1_out, not_2_out, not_3_out, not_4_out, R_type_out;

  not not_1 (not_1_out, Op_0);
  not not_2 (not_2_out, Op1);
  not not_3 (not_3_out, Op3);
  not not_4 (not_4_out, Op2);
  and R_type (R_type_out, not_1_out, not_2_out, not_4_out, not_3_out);
  and LW (MemRead, not_1_out, not_2_out, Op2, Op3);
  and SW (MemWright, Op_0, not_2_out, Op2, Op3);
  and Beq1 (BeqSelect1, not_1_out, Op1, not_4_out, not_3_out);
  and Beq2 (BeqSelect2, Op_0, not_2_out, not_4_out, not_3_out);
  and I_type (I_type_out, Op_0, Op1, Op2, Op3);
  or or_1 (RgDst, R_type_out, BeqSelect2);
  or or_2 (AluSrc, MemRead, MemWright, I_type_out);
  or or_3 (RegWrite, R_type_out, MemRead, I_type_out);
  or or_4 (Branch, BeqSelect1, BeqSelect2);
  or or_5 (AluOp1, R_type_out, MemRead, MemWright, BeqSelect1, BeqSelect2, I_type_out);
  or or_6 (AluOP0, BeqSelect1, BeqSelect2);

  assign MemToReg = MemRead;

  // Notes on the sheet:
  //   Operations   =   op_code
  //   R- Format   =   0000
  //   I- Format   =  1111
  //   Lode (Lw)   =   0011
  //   Store (Sw)   =   1011
  //   Beq1    =   0100
  //   Beq 2    =   1000
endmodule
